// Logisim project PipelinedMips.circ as structural Verilog: 1 circuit, main circuit main
module main (
);

  wire ALUSrc, Branch, clock, ex_mem_1_alu0_2, ex_mem_1_alu1_2, ex_mem_1_alu2_2, ex_mem_1_alusrc_2,
       ex_mem_1_branch_2, ex_mem_1_jump_2, ex_mem_1_memtoreg_2, ex_mem_1_regdest_2, ex_mem_2_lbsignal_2,
       ex_mem_2_memtoreg_2, EX_MEM_RegWrite, hazarddetection_1_stalling_now, ID_EX_lbsignal_2, ID_EX_MemRead,
       ID_EX_memtoreg_2, ID_EX_memwrite_2, ID_EX_regwrote_2, IF_ID_Write, Jump, lbSignal, MemForward,
       MemRead, MemWrite, MemWrite_Dec, or_2_out, PC_Write, PCSrc, RegDest, RegWrite, Squish, Squish_Fetch,
       Stall_Control, Zero, ZeroR;
  wire [1:0] bitRd, bitRs, bitRt, EX_MEM_RD, FA, FB, ID_EX__7_8_2, ID_EX_Rt, IF_ID_Rs, IF_ID_Rt,
       multiplexer_3_out, Rs, WrADDr;
  wire [2:0] ALUctrl, bitFunc, bitOp;
  wire [3:0] bitSa, shmt;
  wire [7:0] multiplexer_8_out;
  wire [8:0] bit0_8;
  wire [11:0] control_unit_aluop_2, multiplexer_1_out;
  wire [12:0] bit0_12, bit0_12_Ex;
  wire [15:0] A, ALU, ALUR, B, bData, Byte, Data, Decode, divider_1_rem, ex_mem_2_alu_2, ex_mem_2_pc_2,
       extend, Jal_value, Mem_Data, multiplexer_4_out, multiplexer_5_out, multiplexer_6_out,
       multiplexer_9_out, PC, PC4, PC_in, PC_l1, PC_L2, PC_plus, RD, RD1, RD2, rom_1_data, shifter_1_out,
       signextend_1_output, subtractor_1_out, WrData;

  Clock clock_1 (.out(clock));
  // Probe on PC_in
  Register #(.width(16)) u_PC (.D(PC_in), .en(PC_Write), .Q(PC), .clk(clock));  // open: clr
  or or_1 (Squish, Jump, PCSrc);
  // Probe on PC
  Adder #(.width(16)) adder_1 (.a(PC), .b(16'h1), .out(PC4));  // open: cin, cout
  ROM #(.dataWidth(16)) rom_1 (.addr(PC[7:0]), .data(rom_1_data));  // open: sel
  IF_ID IF_ID (
    .PC(rom_1_data), .PC_plus(PC4), .Squish(Squish), .IR(Decode), .PC_plus_2(PC_plus),
    .Squish_2(Squish_Fetch), .NotStall(IF_ID_Write), .Clock(clock));
  // Probe on Decode
  // Probe on WrData
  decoder decoder_1 (
    .inst__input(Decode), .bit0_12_func__rs(bit0_12), .bit0_8_func__rd(bit0_8), .bit9_10_rt(bitRt),
    .bit0_2_func(bitFunc), .IF_ID_Rt(IF_ID_Rt), .bit11_12_rs(bitRs), .bit3_6_sa(bitSa), .IF_ID_Rs(IF_ID_Rs),
    .bit13_15_op(bitOp), .bit7_8_rd(bitRd));
  // Probe on WrADDr
  ControlUnit control_unit (
    .ALUop_1(control_unit_aluop_2[1]), .ALUop_0(control_unit_aluop_2[2]), .ALUSrc(control_unit_aluop_2[3]),
    .RegWrite(control_unit_aluop_2[4]), .Jump(control_unit_aluop_2[5]), .RegDst(control_unit_aluop_2[6]),
    .MEMRead(control_unit_aluop_2[7]), .MemToReg(control_unit_aluop_2[8]), .MemWrite(MemWrite_Dec),
    .Branch(control_unit_aluop_2[10]), .I13(bitOp[0]), .I14(bitOp[1]), .I15(bitOp[2]), .I0(bitFunc[0]),
    .I1(bitFunc[1]), .I2(bitFunc[2]), .ALUop_2(control_unit_aluop_2[0]), .lbSignal(control_unit_aluop_2[11]));
  HazardDetection hazarddetection_1 (
    .ID_EX_MemRead(ID_EX_MemRead), .ID_EX_Rt(ID_EX_Rt), .IF_ID_Rs(IF_ID_Rs), .IF_ID_Rt(IF_ID_Rt),
    .LW_Instruction(MemWrite_Dec), .IF_ID_Write(IF_ID_Write), .PC_Write(PC_Write),
    .Stall_Control(Stall_Control), .Stalling_Now(hazarddetection_1_stalling_now));
  // Probe on RD1
  RegFile regfile_1 (
    .WrAddr(WrADDr), .WrReg(RegWrite), .WrData(WrData), .RdAddr1(bitRs), .RdAddr2(bitRt), .RdData1(RD1),
    .RdData2(RD2), .Clock(clock));
  // Probe on bit0_8
  // Probe on hazarddetection_1_stalling_now
  // Probe on RD2
  or or_2 (or_2_out, Squish, Squish_Fetch, Stall_Control);
  Multiplexer #(.width(12), .enable("false")) multiplexer_1 (
    .in0({control_unit_aluop_2[11:10], MemWrite_Dec, control_unit_aluop_2[8:0]}), .in1({12{1'b0}}),
    .out(multiplexer_1_out), .sel(or_2_out));
  SignExtend signextend_1 (.Input(bit0_8), .Output(signextend_1_output));
  // Probe on signextend_1_output
  ID_EX ID_EX (
    .ALU2(multiplexer_1_out[0]), .ALU1(multiplexer_1_out[1]), .Clock(clock), .ALU0(multiplexer_1_out[2]),
    .RegDest(multiplexer_1_out[6]), .Jump(multiplexer_1_out[5]), .Branch(multiplexer_1_out[10]),
    .MemRead(multiplexer_1_out[7]), .MemtoReg(multiplexer_1_out[8]), .MemWrite(multiplexer_1_out[9]),
    .ALUSrc(multiplexer_1_out[3]), .RegWrote(multiplexer_1_out[4]), .lbSignal(multiplexer_1_out[11]),
    .pc(PC_plus), .RD1(RD1), .RD2(RD2), .Exted(signextend_1_output), ._9_10(bitRt), ._7_8(bitRd),
    .SHIFT(bitSa), ._11_12(bitRs), .Bit_0_12(bit0_12), .pc_2(Jal_value), .RD1_2(A), .RD2_2(B),
    .Exted_2(extend), ._7_8_2(ID_EX__7_8_2), .SHIFT_2(shmt), ._11_12_2(Rs), .Bit_0_12_2(bit0_12_Ex),
    .Stall(1'b1), .ALU2_2(ALUctrl[2]), .ALU0_2(ALUctrl[0]), .Jump_2(Jump), .MemRead_2(ID_EX_MemRead),
    .MemWrite_2(ID_EX_memwrite_2), .RegWrote_2(ID_EX_regwrote_2), ._9_10_2(ID_EX_Rt), .ALU1_2(ALUctrl[1]),
    .RegDest_2(RegDest), .Branch_2(Branch), .ALUSrc_2(ALUSrc), .lbSignal_2(ID_EX_lbsignal_2),
    .MemtoReg_2(ID_EX_memtoreg_2));
  // Probe on Jal_value
  Multiplexer #(.select(2), .width(16), .enable("false")) multiplexer_2 (
    .in0(B), .in1(WrData), .in2(ALUR), .out(RD), .sel(FB));  // open: in3
  Subtractor #(.width(16)) subtractor_1 (.a(Jal_value), .b({16{1'b0}}), .out(subtractor_1_out));  // open: bin, bout
  Multiplexer #(.width(2), .enable("false")) multiplexer_3 (
    .in0(ID_EX_Rt), .in1(ID_EX__7_8_2), .out(multiplexer_3_out), .sel(RegDest));
  // Probe on extend
  Multiplexer #(.select(2), .width(16), .enable("false")) multiplexer_4 (
    .in0(A), .in1(WrData), .in2(ALUR), .out(multiplexer_4_out), .sel(FA));  // open: in3
  Multiplexer #(.width(16), .enable("false")) multiplexer_5 (
    .in0(RD), .in1(extend), .out(multiplexer_5_out), .sel(ALUSrc));
  // Probe on extend
  // Probe on {subtractor_1_out[15:13], bit0_12_Ex}
  // Probe on extend
  // Probe on multiplexer_4_out
  // Probe on FA
  ForwardingUnit forwardingunit_1 (
    .ID_EX_RS(Rs), .ID_EX_RT(ID_EX_Rt), .EX_MEM_RegWrite(EX_MEM_RegWrite), .EX_MEM_RegRd(EX_MEM_RD),
    .MEM_WB_RegWrite(RegWrite), .MEM_WB_RegRd(WrADDr), .EX_MEM_MemWr(MemWrite), .ForwardA(FA), .ForwardB(FB),
    .MemForward(MemForward));
  Adder #(.width(16)) adder_2 (.a(Jal_value), .b(extend), .out(PC_l1));  // open: cin, cout
  ALU alu_1 (
    .ALUCtl(ALUctrl), .A(multiplexer_4_out), .B(multiplexer_5_out), .Shamt(shmt), .ALUResult(ALU), .Zero(Zero));  // open: Overflow
  EX_MEM ex_mem_1 (
    .ALU2(ALUctrl[2]), .ALU1(ALUctrl[1]), .clock(clock), .ALU0(ALUctrl[0]), .RegDest(RegDest), .Jump(Jump),
    .Branch(Branch), .MemRead(ID_EX_MemRead), .MemtoReg(ID_EX_memtoreg_2), .MemWrite(ID_EX_memwrite_2),
    .ALUSrc(ALUSrc), .RegWrote(ID_EX_regwrote_2), .lbSignal(ID_EX_lbsignal_2), .pc(PC_l1), .ALU(ALU),
    .RD2(RD), .Zero(Zero), .dest(multiplexer_3_out), .ALU_2(ALUR), .RD2_2(Mem_Data), .Zero_2(ZeroR),
    .dest_2(EX_MEM_RD), .ALU2_2(ex_mem_1_alu2_2), .ALU0_2(ex_mem_1_alu0_2), .Jump_2(ex_mem_1_jump_2),
    .MemRead_2(MemRead), .MemWrite_2(MemWrite), .RegWrote_2(EX_MEM_RegWrite), .ALU1_2(ex_mem_1_alu1_2),
    .RegDest_2(ex_mem_1_regdest_2), .Branch_2(ex_mem_1_branch_2), .ALUSrc_2(ex_mem_1_alusrc_2),
    .lbSignal_2(lbSignal), .MemtoReg_2(ex_mem_1_memtoreg_2), .pc_2(PC_L2));
  Multiplexer #(.width(16), .enable("false")) multiplexer_6 (
    .in0(PC4), .in1(PC_l1), .out(multiplexer_6_out), .sel(PCSrc));
  // Probe on ALU
  // Probe on FB
  Multiplexer #(.width(16), .enable("false")) multiplexer_7 (
    .in0(multiplexer_6_out), .in1({subtractor_1_out[15:13], bit0_12_Ex}), .out(PC_in), .sel(Jump));
  // Probe on PC_in
  Shifter #(.width(16), .shift("lr")) shifter_1 (.in(ALUR), .\dist (4'b0010), .out(shifter_1_out));
  Multiplexer #(.width(8), .enable("false")) multiplexer_8 (
    .in0(ALUR[7:0]), .in1(shifter_1_out[7:0]), .out(multiplexer_8_out), .sel(lbSignal));
  Multiplexer #(.width(16), .enable("false")) multiplexer_9 (
    .in0(Mem_Data), .in1(WrData), .out(multiplexer_9_out), .sel(MemForward));
  and and_1 (PCSrc, Branch, Zero);
  // Probe on multiplexer_9_out
  EX_MEM ex_mem_2 (
    .ALU2(ex_mem_1_alu2_2), .ALU1(ex_mem_1_alu1_2), .clock(clock), .ALU0(ex_mem_1_alu0_2),
    .RegDest(ex_mem_1_regdest_2), .Jump(ex_mem_1_jump_2), .Branch(ex_mem_1_branch_2), .MemRead(MemRead),
    .MemtoReg(ex_mem_1_memtoreg_2), .MemWrite(MemWrite), .ALUSrc(ex_mem_1_alusrc_2),
    .RegWrote(EX_MEM_RegWrite), .lbSignal(lbSignal), .pc(Data), .ALU(ALUR), .dest(EX_MEM_RD),
    .ALU_2(ex_mem_2_alu_2), .dest_2(WrADDr), .RegWrote_2(RegWrite), .lbSignal_2(ex_mem_2_lbsignal_2),
    .MemtoReg_2(ex_mem_2_memtoreg_2), .pc_2(ex_mem_2_pc_2));  // open: RD2, Zero, RD2_2, Zero_2, ALU2_2, ALU0_2, Jump_2, MemRead_2, MemWrite_2, ALU1_2, RegDest_2, Branch_2, ALUSrc_2
  RAM #(.dataWidth(16), .bus("separate")) ram_1 (
    .addr(multiplexer_8_out), .din(multiplexer_9_out), .data(Data), .str(MemWrite), .clk(clock), .ld(MemRead));  // open: sel, clr
  Multiplexer #(.width(16), .enable("false")) multiplexer_10 (
    .in0(ex_mem_2_alu_2), .in1(ex_mem_2_pc_2), .out(bData), .sel(ex_mem_2_memtoreg_2));
  Divider #(.width(16)) divider_1 (.a(ex_mem_2_alu_2), .b(16'h4), .rem(divider_1_rem));  // open: out, upper
  Multiplexer #(.width(16), .enable("false")) multiplexer_11 (
    .in0(bData), .in1({{13{Byte[15]}}, Byte[2:0]}), .out(WrData), .sel(ex_mem_2_lbsignal_2));
  // Probe on PC
  // Probe on Branch
  // Probe on Jump
  // Probe on RegWrite
  // Probe on WrADDr
  // Probe on WrData
  // Probe on MemWrite
  // Probe on Mem_Data
  Multiplexer #(.select(2), .width(4), .enable("false")) multiplexer_12 (
    .in0(bData[3:0]), .in1(bData[7:4]), .in2(bData[11:8]), .in3(bData[15:12]), .out({Byte[15], Byte[2:0]}),
    .sel(divider_1_rem[1:0]));

  // Other names for the same wires on the sheet: Byte[14:3] = {12{Byte[15]}}; PC_r[15:0] = Jal_value

  // Notes on the sheet:
  //   NOTE:
  //   Only Instruction 2-8 taken
  //   contents of rom_1 (hex, n*v repeats v):
  //   8200 6200 8201 6201 8202 6202 8203 6203 8204 6204 8205 6205 8405 8600 5200 f82 95ff 1087 23fb 6600
endmodule
