// Logisim project components.circ as structural Verilog
module RegFile (
  input  [1:0] WrAddr,
  input  WrReg,
  input  [15:0] WrData,
  input  [1:0] RdAddr1,
  input  [1:0] RdAddr2,
  input  Clock,
  output [15:0] RdData1,
  output [15:0] RdData2
);

  wire and_1_out, and_2_out, comparator_1_eq, comparator_2_eq, comparator_3_eq, comparator_4_eq, not_1_out,
       not_2_out, WrReg0, WrReg1, WrReg2, WrReg3;
  wire [15:0] multiplexer_1_out, multiplexer_2_out, RegData1, RegData2, RegData3;

  Demultiplexer #(.select(2), .enable("false")) demultiplexer_1 (
    .out0(WrReg0), .out1(WrReg1), .out2(WrReg2), .out3(WrReg3), .in(WrReg), .sel(WrAddr));
  Register #(.width(16)) register_1 (.D(WrData), .en(WrReg1), .Q(RegData1), .clk(Clock));  // open: clr
  Register #(.width(16)) register_2 (.D(WrData), .en(WrReg2), .Q(RegData2), .clk(Clock));  // open: clr
  Register #(.width(16)) register_3 (.D(WrData), .en(WrReg3), .Q(RegData3), .clk(Clock));  // open: clr
  Multiplexer #(.select(2), .width(16), .enable("false")) multiplexer_1 (
    .in0({16{1'b0}}), .in1(RegData1), .in2(RegData2), .in3(RegData3), .out(multiplexer_1_out), .sel(RdAddr1));
  Multiplexer #(.select(2), .width(16), .enable("false")) multiplexer_2 (
    .in0({16{1'b0}}), .in1(RegData1), .in2(RegData2), .in3(RegData3), .out(multiplexer_2_out), .sel(RdAddr2));
  Comparator #(.width(2)) comparator_1 (.a(WrAddr), .b(RdAddr1), .eq(comparator_1_eq));  // open: gt, lt
  and and_1 (and_1_out, comparator_1_eq, WrReg, not_1_out);
  Multiplexer #(.width(16), .enable("false")) multiplexer_3 (
    .in0(multiplexer_1_out), .in1(WrData), .out(RdData1), .sel(and_1_out));
  Comparator #(.width(2)) comparator_2 (.a(WrAddr), .b(RdAddr2), .eq(comparator_2_eq));  // open: gt, lt
  and and_2 (and_2_out, comparator_2_eq, WrReg, not_2_out);
  Multiplexer #(.width(16), .enable("false")) multiplexer_4 (
    .in0(multiplexer_2_out), .in1(WrData), .out(RdData2), .sel(and_2_out));
  Comparator #(.width(2)) comparator_3 (.a(WrAddr), .b(2'b00), .eq(comparator_3_eq));  // open: gt, lt
  Comparator #(.width(2)) comparator_4 (.a(WrAddr), .b(2'b00), .eq(comparator_4_eq));  // open: gt, lt
  not not_1 (not_1_out, comparator_3_eq);
  not not_2 (not_2_out, comparator_4_eq);
endmodule

module ID_EX (
  input  Stall,
  input  ALU2,
  input  ALU1,
  input  Clock,
  input  ALU0,
  input  RegDest,
  input  Jump,
  input  Branch,
  input  MemRead,
  input  MemtoReg,
  input  MemWrite,
  input  ALUSrc,
  input  RegWrote,
  input  lbSignal,
  input  [15:0] pc,
  input  [15:0] RD1,
  input  [15:0] RD2,
  input  [15:0] Exted,
  input  [1:0] _9_10,
  input  [1:0] _7_8,
  input  [3:0] SHIFT,
  input  [1:0] _11_12,
  input  [12:0] Bit_0_12,
  output ALU2_2,
  output ALU1_2,
  output ALU0_2,
  output RegDest_2,
  output Jump_2,
  output Branch_2,
  output MemRead_2,
  output MemtoReg_2,
  output MemWrite_2,
  output ALUSrc_2,
  output RegWrote_2,
  output lbSignal_2,
  output [15:0] pc_2,
  output [15:0] RD1_2,
  output [15:0] RD2_2,
  output [15:0] Exted_2,
  output [1:0] _9_10_2,
  output [1:0] _7_8_2,
  output [3:0] SHIFT_2,
  output [1:0] _11_12_2,
  output [12:0] Bit_0_12_2
);

  Register #(.width(1)) register_1 (.D(ALU2), .en(Stall), .Q(ALU2_2), .clk(Clock));  // open: clr
  Register #(.width(1)) register_2 (.D(ALU0), .en(Stall), .Q(ALU0_2), .clk(Clock));  // open: clr
  Register #(.width(1)) register_3 (.D(Jump), .en(Stall), .Q(Jump_2), .clk(Clock));  // open: clr
  Register #(.width(1)) register_4 (.D(MemRead), .en(Stall), .Q(MemRead_2), .clk(Clock));  // open: clr
  Register #(.width(1)) register_5 (.D(MemWrite), .en(Stall), .Q(MemWrite_2), .clk(Clock));  // open: clr
  Register #(.width(1)) register_6 (.D(RegWrote), .en(Stall), .Q(RegWrote_2), .clk(Clock));  // open: clr
  Register #(.width(16)) u_PC (.D(pc), .en(Stall), .Q(pc_2), .clk(Clock));  // open: clr
  Register #(.width(2)) u__9_10 (.D(_9_10), .en(Stall), .Q(_9_10_2), .clk(Clock));  // open: clr
  Register #(.width(4)) u_SHIFT (.D(SHIFT), .en(Stall), .Q(SHIFT_2), .clk(Clock));  // open: clr
  Register #(.width(2)) u__11_12 (.D(_11_12), .en(Stall), .Q(_11_12_2), .clk(Clock));  // open: clr
  Register #(.width(13)) _0_12 (.D(Bit_0_12), .en(Stall), .Q(Bit_0_12_2), .clk(Clock));  // open: clr
  Register #(.width(16)) u_RD1 (.D(RD1), .en(Stall), .Q(RD1_2), .clk(Clock));  // open: clr
  Register #(.width(16)) Extend (.D(Exted), .en(Stall), .Q(Exted_2), .clk(Clock));  // open: clr
  Register #(.width(1)) register_7 (.D(ALU1), .en(Stall), .Q(ALU1_2), .clk(Clock));  // open: clr
  Register #(.width(1)) register_8 (.D(RegDest), .en(Stall), .Q(RegDest_2), .clk(Clock));  // open: clr
  Register #(.width(1)) register_9 (.D(Branch), .en(Stall), .Q(Branch_2), .clk(Clock));  // open: clr
  Register #(.width(1)) register_10 (.D(MemtoReg), .en(Stall), .Q(MemtoReg_2), .clk(Clock));  // open: clr
  Register #(.width(1)) register_11 (.D(ALUSrc), .en(Stall), .Q(ALUSrc_2), .clk(Clock));  // open: clr
  Register #(.width(1)) register_12 (.D(lbSignal), .en(Stall), .Q(lbSignal_2), .clk(Clock));  // open: clr
  Register #(.width(16)) u_RD2 (.D(RD2), .en(Stall), .Q(RD2_2), .clk(Clock));  // open: clr
  Register #(.width(2)) u__7_8 (.D(_7_8), .en(Stall), .Q(_7_8_2), .clk(Clock));  // open: clr
endmodule

module IF_ID (
  input  NotStall,
  input  [15:0] PC,
  input  Clock,
  input  [15:0] PC_plus,
  input  Squish,
  output [15:0] IR,
  output [15:0] PC_plus_2,
  output Squish_2
);

  // Probe on PC
  // Probe on IR
  Register #(.width(16)) u_IR (.D(PC), .en(NotStall), .Q(IR), .clk(Clock));  // open: clr
  Register #(.width(16)) PC_4 (.D(PC_plus), .en(NotStall), .Q(PC_plus_2), .clk(Clock));  // open: clr
  Register #(.width(1)) u_Squish (.D(Squish), .Q(Squish_2), .clk(Clock));  // open: en, clr
endmodule

module EX_MEM (
  input  ALU2,
  input  ALU1,
  input  clock,
  input  ALU0,
  input  RegDest,
  input  Jump,
  input  Branch,
  input  MemRead,
  input  MemtoReg,
  input  MemWrite,
  input  ALUSrc,
  input  RegWrote,
  input  lbSignal,
  input  [15:0] pc,
  input  [15:0] ALU,
  input  [15:0] RD2,
  input  Zero,
  input  [1:0] dest,
  output ALU2_2,
  output ALU1_2,
  output ALU0_2,
  output RegDest_2,
  output Jump_2,
  output Branch_2,
  output MemRead_2,
  output MemtoReg_2,
  output MemWrite_2,
  output ALUSrc_2,
  output RegWrote_2,
  output lbSignal_2,
  output [15:0] pc_2,
  output [15:0] ALU_2,
  output [15:0] RD2_2,
  output Zero_2,
  output [1:0] dest_2
);

  Register #(.width(1)) register_1 (.D(ALU2), .Q(ALU2_2), .clk(clock));  // open: en, clr
  Register #(.width(1)) register_2 (.D(ALU0), .Q(ALU0_2), .clk(clock));  // open: en, clr
  Register #(.width(1)) register_3 (.D(Jump), .Q(Jump_2), .clk(clock));  // open: en, clr
  Register #(.width(1)) register_4 (.D(MemRead), .Q(MemRead_2), .clk(clock));  // open: en, clr
  Register #(.width(1)) register_5 (.D(MemWrite), .Q(MemWrite_2), .clk(clock));  // open: en, clr
  Register #(.width(1)) register_6 (.D(RegWrote), .Q(RegWrote_2), .clk(clock));  // open: en, clr
  Register #(.width(16)) u_PC (.D(pc), .Q(pc_2), .clk(clock));  // open: en, clr
  Register #(.width(16)) u_ALU (.D(ALU), .Q(ALU_2), .clk(clock));  // open: en, clr
  Register #(.width(1)) Extend (.D(Zero), .Q(Zero_2), .clk(clock));  // open: en, clr
  Register #(.width(2)) u_dest (.D(dest), .Q(dest_2), .clk(clock));  // open: en, clr
  Register #(.width(1)) register_7 (.D(ALU1), .Q(ALU1_2), .clk(clock));  // open: en, clr
  Register #(.width(1)) register_8 (.D(RegDest), .Q(RegDest_2), .clk(clock));  // open: en, clr
  Register #(.width(1)) register_9 (.D(Branch), .Q(Branch_2), .clk(clock));  // open: en, clr
  Register #(.width(1)) register_10 (.D(MemtoReg), .Q(MemtoReg_2), .clk(clock));  // open: en, clr
  Register #(.width(1)) register_11 (.D(ALUSrc), .Q(ALUSrc_2), .clk(clock));  // open: en, clr
  Register #(.width(1)) register_12 (.D(lbSignal), .Q(lbSignal_2), .clk(clock));  // open: en, clr
  Register #(.width(16)) u_RD2 (.D(RD2), .Q(RD2_2), .clk(clock));  // open: en, clr
endmodule

module ForwardingUnit (
  input  [1:0] ID_EX_RS,
  input  [1:0] ID_EX_RT,
  input  EX_MEM_RegWrite,
  input  [1:0] EX_MEM_RegRd,
  input  MEM_WB_RegWrite,
  input  [1:0] MEM_WB_RegRd,
  input  EX_MEM_MemWr,
  output [1:0] ForwardA,
  output [1:0] ForwardB,
  output MemForward
);

  wire comparator_1_eq, comparator_2_eq, comparator_3_eq, comparator_4_eq, comparator_5_eq, comparator_6_eq,
       comparator_7_eq, comparator_8_eq, comparator_9_eq, not_1_out, not_2_out, not_3_out, not_4_out,
       not_5_out, not_6_out;

  Comparator #(.width(2)) comparator_1 (.a(MEM_WB_RegRd), .b(EX_MEM_RegRd), .eq(comparator_1_eq));  // open: gt, lt
  Comparator #(.width(2)) comparator_2 (.a(EX_MEM_RegRd), .b(ID_EX_RT), .eq(comparator_2_eq));  // open: gt, lt
  Comparator #(.width(2)) comparator_3 (.a(EX_MEM_RegRd), .b(2'b00), .eq(comparator_3_eq));  // open: gt, lt
  Comparator #(.width(2)) comparator_4 (.a(MEM_WB_RegRd), .b(ID_EX_RT), .eq(comparator_4_eq));  // open: gt, lt
  Comparator #(.width(2)) comparator_5 (.a(MEM_WB_RegRd), .b(2'b00), .eq(comparator_5_eq));  // open: gt, lt
  Comparator #(.width(2)) comparator_6 (.a(EX_MEM_RegRd), .b(2'b00), .eq(comparator_6_eq));  // open: gt, lt
  not not_1 (not_1_out, comparator_6_eq);
  Comparator #(.width(2)) comparator_7 (.a(EX_MEM_RegRd), .b(ID_EX_RS), .eq(comparator_7_eq));  // open: gt, lt
  Comparator #(.width(2)) comparator_8 (.a(ID_EX_RS), .b(MEM_WB_RegRd), .eq(comparator_8_eq));  // open: gt, lt
  Comparator #(.width(2)) comparator_9 (.a(MEM_WB_RegRd), .b(2'b00), .eq(comparator_9_eq));  // open: gt, lt
  not not_2 (not_2_out, comparator_9_eq);
  not not_3 (not_3_out, comparator_3_eq);
  not not_4 (not_4_out, ForwardB[1]);
  not not_5 (not_5_out, comparator_5_eq);
  not not_6 (not_6_out, ForwardA[1]);
  and and_1 (ForwardA[1], EX_MEM_RegWrite, not_1_out, comparator_7_eq);
  and and_2 (ForwardA[0], not_6_out, MEM_WB_RegWrite, comparator_8_eq, not_2_out);
  and and_3 (ForwardB[1], EX_MEM_RegWrite, comparator_2_eq, not_3_out);
  and and_4 (ForwardB[0], not_4_out, comparator_4_eq, not_5_out, MEM_WB_RegWrite);
  and and_5 (MemForward, not_5_out, comparator_1_eq, MEM_WB_RegWrite, EX_MEM_MemWr);
endmodule

module HazardDetection (
  input  ID_EX_MemRead,
  input  [1:0] ID_EX_Rt,
  input  [1:0] IF_ID_Rs,
  input  [1:0] IF_ID_Rt,
  input  LW_Instruction,
  output IF_ID_Write,
  output PC_Write,
  output Stall_Control,
  output Stalling_Now
);

  wire and_1_out, comparator_1_eq, comparator_2_eq, not_1_out, or_1_out;

  not not_1 (not_1_out, LW_Instruction);
  Comparator #(.width(2)) comparator_1 (.a(ID_EX_Rt), .b(IF_ID_Rs), .eq(comparator_1_eq));  // open: gt, lt
  Comparator #(.width(2)) comparator_2 (.a(ID_EX_Rt), .b(IF_ID_Rt), .eq(comparator_2_eq));  // open: gt, lt
  or or_1 (or_1_out, comparator_1_eq, and_1_out);
  and and_1 (and_1_out, comparator_2_eq, not_1_out);
  and and_2 (Stall_Control, ID_EX_MemRead, or_1_out);
  not not_2 (IF_ID_Write, Stall_Control);

  assign PC_Write = IF_ID_Write;
  assign Stalling_Now = Stall_Control;

  // Notes on the sheet:
  //   The Not gate is there for the two Write signals because, in all other cases we want the registered to be ENABLED which are driven by these..
endmodule

module ControlUnit (
  input  I13,
  input  I14,
  input  I15,
  input  I2,
  input  I1,
  input  I0,
  output ALUop_2,
  output ALUop_1,
  output ALUop_0,
  output ALUSrc,
  output RegWrite,
  output Jump,
  output RegDst,
  output MEMRead,
  output MemToReg,
  output MemWrite,
  output Branch,
  output lbSignal
);

  wire and_1_out, and_2_out, and_3_out, nor_1_out, nor_2_out, not_1_out, not_2_out, not_3_out, not_4_out,
       not_5_out, not_6_out;
  wire [1:0] and_4_out;
  wire [2:0] multiplexer_1_out;

  not not_1 (not_1_out, I14);
  nor nor_1 (nor_1_out, I15, I14);
  not not_2 (not_2_out, I14);
  not not_3 (not_3_out, I13);
  not not_4 (not_4_out, I13);
  not not_5 (not_5_out, I15);
  and and_1 (and_1_out, I15, I14);
  not not_6 (not_6_out, I13);
  and and_2 (and_2_out, I15, I13, not_1_out);
  and and_3 (and_3_out, I15, not_2_out);
  nor nor_2 (nor_2_out, I15, I14);
  Multiplexer #(.width(3), .enable("false")) multiplexer_1 (
    .in0(3'b010), .in1(3'b101), .out(multiplexer_1_out), .sel(and_2_out));
  nor nor_3 (and_4_out[1], I15, I14, I13);
  and and_4 (and_4_out[0], I13, nor_1_out);
  or or_1 (ALUSrc, I15, I14);
  or or_2 (RegWrite, and_3_out, not_3_out);
  and and_5 (Jump, I15, I14, I13);
  nor nor_4 (RegDst, I15, I14, I13);
  and and_6 (MEMRead, I14, not_4_out);
  and and_7 (MemWrite, not_5_out, I14, I13);
  and and_8 (Branch, nor_2_out, I13);
  and and_9 (lbSignal, and_1_out, not_6_out);
  Multiplexer #(.select(2), .width(3), .enable("false")) multiplexer_2 (
    .in0(multiplexer_1_out), .in1(3'b110), .in2({I2, I1, I0}), .in3(3'b000),
    .out({ALUop_2, ALUop_1, ALUop_0}), .sel(and_4_out));

  assign MemToReg = MEMRead;

  // Notes on the sheet:
  //   Add
  //   Lui
  //   ALUop 1
  //   ALUop 0
  //   Branch
  //   Sub
endmodule

module SignExtend (
  input  [8:0] Input,
  output [15:0] Output
);


  assign Output = {{8{Input[8]}}, Input[7:0]};
endmodule

module ShiftLeft2 (
  input  [15:0] Input,
  output [15:0] Output
);


  assign Output = {Input[13:0], 2'b00};
endmodule

module _32bit (
  input  Add_Sub_control,
  input  [15:0] in_2,
  input  [15:0] in_3,
  output [15:0] out_4,
  output carry_out
);

  wire adder_1_cout, subtractor_1_bout;
  wire [15:0] adder_1_out, subtractor_1_out;

  Adder #(.width(16)) adder_1 (.a(in_2), .b(in_3), .out(adder_1_out), .cout(adder_1_cout));  // open: cin
  Subtractor #(.width(16)) subtractor_1 (
    .a(in_2), .b(in_3), .out(subtractor_1_out), .bout(subtractor_1_bout));  // open: bin
  Multiplexer #(.width(16), .enable("false")) multiplexer_1 (
    .in0(adder_1_out), .in1(subtractor_1_out), .out(out_4), .sel(Add_Sub_control));
  Multiplexer #(.enable("false")) multiplexer_2 (
    .in0(adder_1_cout), .in1(subtractor_1_bout), .out(carry_out), .sel(Add_Sub_control));
endmodule

module ALU (
  input  [2:0] ALUCtl,
  input  [15:0] A,
  input  [15:0] B,
  input  [3:0] Shamt,
  output [15:0] ALUResult,
  output Zero,
  output Overflow
);

  wire and_2_out, and_3_out, comparator_1_lt, not_1_out, not_2_out, not_3_out, or_2_out;
  wire [15:0] Add, And, LessThan, lui, Nor, Or, ShiftLeft, ShiftRight, Sub;

  Adder #(.width(16)) adder_1 (.a(A), .b(B), .out(Add));  // open: cin, cout
  Subtractor #(.width(16)) subtractor_1 (.a(A), .b(B), .out(Sub));  // open: bin, bout
  assign And = A & B;  // AND_Gate and_1, 16 bits wide
  assign Or = A | B;  // OR_Gate or_1, 16 bits wide
  assign Nor = ~(A | B);  // NOR_Gate nor_1, 16 bits wide
  Comparator #(.width(16)) comparator_1 (.a(A), .b(B), .lt(comparator_1_lt));  // open: gt, eq
  Shifter #(.width(16)) shifter_1 (.in(B), .\dist (Shamt), .out(ShiftLeft));
  Shifter #(.width(16), .shift("lr")) shifter_2 (.in(B), .\dist (Shamt), .out(ShiftRight));
  Shifter #(.width(16)) shifter_3 (.in(B), .\dist (4'b0111), .out(lui));
  assign LessThan = {{15{1'b0}}, comparator_1_lt};  // Bit_Extender bit_extender_1
  not not_1 (not_1_out, ALUCtl[0]);
  not not_2 (not_2_out, ALUCtl[1]);
  not not_3 (not_3_out, ALUCtl[2]);
  Multiplexer #(.select(3), .width(16), .enable("false")) multiplexer_1 (
    .in0(And), .in1(Or), .in2(Add), .in3(ShiftLeft), .in4(ShiftRight), .in5(lui), .in6(Sub), .in7(LessThan),
    .out(ALUResult), .sel(ALUCtl));
  and and_2 (and_2_out, not_1_out, not_2_out, ALUCtl[2]);
  and and_3 (and_3_out, not_1_out, ALUCtl[1], not_3_out);
  Overflow overflow_1 (
    .Add(and_2_out), .Sub(and_3_out), .ASign(A[15]), .BSign(B[15]), .ResultSign(ALUResult[15]),
    .Overflow(Overflow));
  not not_4 (Zero, or_2_out);
  or or_2 (or_2_out, ALUResult[0], ALUResult[1], ALUResult[2], ALUResult[3], ALUResult[4], ALUResult[5], ALUResult[6], ALUResult[7], ALUResult[8], ALUResult[9], ALUResult[10], ALUResult[11], ALUResult[12], ALUResult[13], ALUResult[14], ALUResult[15]);

  // Other names for the same wires on the sheet: ASign = A[15]; ResultSign = ALUResult[15]; BSign = B[15]
endmodule

module Overflow (
  input  Add,
  input  Sub,
  input  ASign,
  input  BSign,
  input  ResultSign,
  output Overflow
);

  wire and_1_out, and_2_out, or_1_out, xnor_1_out, xor_1_out, xor_2_out;

  xnor xnor_1 (xnor_1_out, ASign, BSign);
  xor xor_1 (xor_1_out, ASign, BSign);
  and and_1 (and_1_out, xnor_1_out, Add);
  and and_2 (and_2_out, xor_1_out, Sub);
  or or_1 (or_1_out, and_1_out, and_2_out);
  xor xor_2 (xor_2_out, ResultSign, ASign);
  and and_3 (Overflow, or_1_out, xor_2_out);

  // Notes on the sheet:
  //   Overflow occurs when doing addition and sign(A) == sign(B) && sign(result) != sign(A)
  //   Or
  //   Overflow occurs when doing subtraction and sign(A) != sign(B) && sign(result) != sign(A)
endmodule

module Add (
  input  [15:0] A,
  input  [15:0] B,
  output [15:0] Output,
  output Overflow
);

  wire alu_1_p1;

  // ALU alu_1: pin names not known; wires that end beside it: alu_1_p1, A, B, 4'b0000, alu_1_p1, 3'b100, Output, Overflow

  // Notes on the sheet:
  //   ADD function: 101
endmodule
