// Logisim project decoder.circ as structural Verilog: 1 circuit, main circuit decoder
module decoder (
  input  [15:0] inst__input,
  output [12:0] bit0_12_func__rs,
  output [8:0] bit0_8_func__rd,
  output [1:0] bit9_10_rt,
  output [2:0] bit0_2_func,
  output [1:0] IF_ID_Rt,
  output [1:0] bit11_12_rs,
  output [3:0] bit3_6_sa,
  output [1:0] IF_ID_Rs,
  output [2:0] bit13_15_op,
  output [1:0] bit7_8_rd
);


  assign bit0_2_func = inst__input[2:0];
  assign bit0_8_func__rd = inst__input[8:0];
  assign bit0_12_func__rs = inst__input[12:0];
  assign bit3_6_sa = inst__input[6:3];
  assign bit7_8_rd = inst__input[8:7];
  assign bit9_10_rt = inst__input[10:9];
  assign bit11_12_rs = inst__input[12:11];
  assign bit13_15_op = inst__input[15:13];
  assign IF_ID_Rs = inst__input[12:11];
  assign IF_ID_Rt = inst__input[10:9];
endmodule
